# Fritzing sketch Untitled Sketch 2 (saved by Fritzing 0.9.3b)
breadboards: 1

parts:
  U1 = NodeMCU V1.0
  Part1 = Arduino Uno (Rev3) - ICSP
  HC-SR04_Sensor_1 = HC-SR04 Ultrasonic Distance Sensor
  HC-SR04_Sensor_2 = HC-SR04 Ultrasonic Distance Sensor
  Part2 = LCD1602-I2C
  SERVO1 = Tower Pro SG90 servo [part_number=101246]

nets:
  GND: U1.GND, Part1.GND
  N1: U1.RX, Part1.D3_PWM
  N2: U1.TX, Part1.D2
  N3: Part1.A4/SDA, Part2.SDA
  N4: Part1.A5/SCL, Part2.SCL
  N5: Part1.D9_PWM, HC-SR04_Sensor_2.ECHO
  N6: Part1.D10_PWM/SS, HC-SR04_Sensor_2.TRIG
  N7: Part1.D12/MISO, HC-SR04_Sensor_1.TRIG
  N8: Part1.D13/SCK, HC-SR04_Sensor_1.ECHO
  N9: Part1.D6_PWM, SERVO1.Signal
  VCC: HC-SR04_Sensor_1.VCC, HC-SR04_Sensor_2.VCC, Part2.VCC, SERVO1.+5V
  GND_2: HC-SR04_Sensor_1.GND, HC-SR04_Sensor_2.GND, Part2.GND, SERVO1.GND

custom parts:
  NodeMCU V1.0: ESP8266 based NodeMCU
  LCD1602-I2C: A standard character display, usually with 2x16 characters. Comes in many colors with LCM1602 IIC attached.
  Tower Pro SG90 servo: Original file by John De Cristofaro http://www.adafruit.com/products/1449 Adafruit Feedback Servo (Small) Edited by: e-radionica.com 28/9/2015
