# Fritzing sketch Untitled Sketch 4 (saved by Fritzing 0.9.3b)

parts:
  U1 = NodeMCU V1.0
  MQ135 = Gas Sensor Breakout Board

nets:
  GND: U1.GND, MQ135.GND
  VIN: U1.Vin, MQ135.5V
  N1: U1.A0, MQ135.AOUT

custom parts:
  NodeMCU V1.0: ESP8266 based NodeMCU
  Gas Sensor Breakout Board: Gas sensor breakout board. Input voltage is 5V. Sensor output is available in analog and digital.
